# Fritzing sketch WatchTheClock_wiring (saved by Fritzing 0.9.3b)

parts:
  X1 = X113647 Stepper Driver Board [package=board]
  hc-sr1 = hc-sr04
  MOTOR1 = 28BYJ-48 Stepper Motor  # not connected
  U1 = ESP32S-HiLetgo [part_number=ESP32S-HiLetgo]
  S1 = Square Pushbutton

nets:
  N1: X1.IN1, U1.GPIO6
  N2: X1.IN2, U1.GPIO7
  N3: X1.IN3, U1.GPIO8
  N4: X1.IN4, U1.GPIO15
  N5: hc-sr1.VCC, U1.GPIO11
  N6: hc-sr1.Trig, U1.GPIO10
  N7: hc-sr1.Echo, U1.GPIO9
  GND: hc-sr1.GND, U1.VIN
  N8: U1.GND, S1.leg0
  N9: U1.GPIO16, S1.leg1

custom parts:
  X113647 Stepper Driver Board: A common stepper motor driver board based on ULN2003APG darlington array
  ESP32S-HiLetgo: HiLetgo ESP-WROOM-32 ESP32 ESP-32S Development Board 2.4GHz Dual-Mode WiFi + Bluetooth Dual Cores Microcontroller The ESP32 integrated with Antenna switches, RF Balun, power amplifiers, low-noise amplifiers, filters, and management modules, and the entire solution occupies the least area of PCB. 2.4 GHz Wi-Fi plus Bluetooth dual-mode chip, with TSMC Ultra-low power consumption 40nm technology,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
